// Digital circuit AllComponents.dig as structural Verilog
module AllComponents (
  input  [7:0] in8,
  input  in1,
  input  in1b,
  input  clk,
  input  [3:0] in4,
  input  [1:0] in2,
  input  [15:0] in_8,
  output U
);

  wire diodeforward_1_out, not_2_out, notconnected_1_out, pullup_1_out;

  // NotConnected on notconnected_1_out
  PowerSupply powersupply_1 (.VDD(1'b1), .GND(1'b0));
  // ButtonLED buttonled_1: pin names not known; wires that end beside it: in1b
  Button button_1 ();  // open: out
  // RotEncoder rotencoder_1: pin names not known; wires that end beside it: notconnected_1_out
  Reset reset_1 ();  // open: out
  DipSwitch dipswitch_1 ();  // open: out
  // StepperMotorBipolar steppermotorbipolar_1: pin names not known; wires that end beside it: 1'b1, in1, in1, in1, in1, in1, in1, in1, in1, in1
  // And and_1 has open pins: In_1=in1, In_2=in1b, out=open
  // NAnd nand_1 has open pins: In_1=in1, In_2=in1b, out=open
  // Or or_1 has open pins: In_1=in1, In_2=in1b, out=open
  // NOr nor_1 has open pins: In_1=in1, In_2=in1b, out=open
  // XOr xor_1 has open pins: In_1=in1, In_2=in1b, out=open
  // XNOr xnor_1 has open pins: In_1=in1, In_2=in1b, out=open
  // Not not_1 has open pins: in=in1, out=open
  LookUpTable lookuptable_1 (.in0(in1), .in1(in1b));  // open: out
  Delay delay_1 (.in(in1));  // open: out
  // MIDI midi_1: pin names not known; wires that end beside it: 7'b0000001, 7'b0000001, in1, in1, in1
  // StepperMotorUnipolar steppermotorunipolar_1: pin names not known
  LED led_1 (.in(in1));
  // Probe on in1
  LightBulb lightbulb_1 (.A(in1), .B(in1));
  Seven_Seg seven_seg_1 (.a(in1), .b(in1), .c(in1), .d(in1), .e(in1), .f(in1), .g(in1), .dp(in1));
  Seven_Seg_Hex seven_seg_hex_1 (.d(in4), .dp(in1));
  Keyboard keyboard_1 (.C(in1), .en(in1));  // open: D, av
  Terminal terminal_1 (.D(in8), .C(in1), .en(in1));
  Stop stop_1 (.stop(in1));
  PRNG #(.Bits(8)) prng_1 (.S(in8), .se(in1), .ne(in1), .C(in1));  // open: R
  // Gdb gdb_1: pin names not known; wires that end beside it: in1
  // GdbJtag gdbjtag_1: pin names not known
  LedMatrix #(.colAddrBits(4)) ledmatrix_1 (.rows(in8), .column(in4));
  Telnet #(.port(2323)) telnet_1 (.in(in8), .C(in1), .wr(in1), .rd(in1));  // open: out, av
  Multiplexer #(.Bits(4)) multiplexer_1 (.sel(in1), .in_0(in4), .in_1(in4));  // open: out
  Demultiplexer demultiplexer_1 (.sel(in1), .in(in1));  // open: out_0, out_1
  Decoder decoder_1 (.sel(in1));  // open: out_0, out_1
  PriorityEncoder priorityencoder_1 (.in0(in1), .in1(in1));  // open: num, any
  VGA vga_1 (.R(in1), .G(in1), .B(in1), .H(in1), .V(in1), .C(in1));
  BusSplitter #(.Bits(4)) bussplitter_1 (.D(in4), .OE(in1), .D0(in1), .D1(in1), .D2(in1), .D3(in1));
  Driver #(.Bits(4)) driver_1 (.in(in4), .en(in1));  // open: out
  DriverInvSel #(.Bits(4)) driverinvsel_1 (.in(in4), .en(in1));  // open: out
  BitSelector #(.Selector_Bits(2)) bitselector_1 (.in(in4), .sel(in2));  // open: out
  // PinControl #(.Bits(8)) pincontrol_1: pin names not known; wires that end beside it: in8, in1, in8, in8
  JK_FF jk_ff_1 (.J(in1), .C(clk), .K(in1));  // open: Q, nQ
  D_FF d_ff_1 (.D(in1), .C(clk));  // open: Q, nQ
  T_FF t_ff_1 (.T(in1), .C(clk));  // open: Q, nQ
  ROM #(.AddrBits(8), .Bits(8)) rom_1 (.A(in8), .sel(in1));  // open: D
  ROMDualPort #(.AddrBits(8), .Bits(8)) romdualport_1 (.A1(in8), .s1(in1), .A2(in8), .s2(in1));  // open: D1, D2
  GraphicCard #(.graphicHeight(10), .graphicWidth(10), .Bits(8)) graphiccard_1 (
    .A(in8), .str(in1), .C(clk), .ld(in1), .B(in1), .D(in8));
  SixteenSeg sixteenseg_1 (.led(in_8), .dp(in1));
  // ScopeTrigger scopetrigger_1: pin names not known; wires that end beside it: in1
  Add #(.Bits(8)) add_1 (.a(in8), .b(in8), .c_i(in1));  // open: s, c_o
  Sub #(.Bits(8)) sub_1 (.a(in8), .b(in8), .c_i(in1));  // open: s, c_o
  Mul #(.Bits(8)) mul_1 (.a(in8), .b(in8));  // open: mul
  Div #(.Bits(8)) div_1 (.a(in8), .b(in8));  // open: q, r
  BarrelShifter #(.Bits(8)) barrelshifter_1 (.in(in8), .shift(in4));  // open: out
  Comparator #(.Bits(8)) comparator_1 (.a(in8), .b(in8));  // open: gt, eq, lt
  Neg #(.Bits(8)) neg_1 (.in(in8));  // open: out
  BitExtender bitextender_1 (.in(in8));  // open: out
  BitCount #(.Bits(8)) bitcount_1 (.in(in8));  // open: out
  // Relay relay_1: pin names not known; wires that end beside it: in1, in1, in1, in1, in1, in1
  // RelayDT relaydt_1: pin names not known; wires that end beside it: in1, in1, in1, in1
  Switch switch_1 (.A(in1), .B(in1));
  // SwitchDT switchdt_1: pin names not known; wires that end beside it: in1, in1, in1
  Fuse fuse_1 (.A(in1), .B(in1));
  PFET pfet_1 (.G(in1), .S(in1), .D(in1));
  NFET nfet_1 (.G(in1), .D(in1), .S(in1));
  FGPFET fgpfet_1 (.G(in1), .S(in1), .D(in1));
  FGNFET fgnfet_1 (.G(in1), .D(in1), .S(in1));
  TransGate transgate_1 (.A(in1), .nA(not_2_out), .out1(in1), .out2(in1));
  Break break_1 (.brk(in1));
  DiodeForward diodeforward_1 (.in(in1), .out(diodeforward_1_out));
  PullDown pulldown_1 (.out(diodeforward_1_out));
  PullUp pullup_1 (.out(pullup_1_out));
  DiodeBackward diodebackward_1 (.in(in1), .out(pullup_1_out));
  not not_2 (not_2_out, in1);
  // PolarityAwareLED polarityawareled_1: pin names not known; wires that end beside it: in1, in1
  // RGBLED rgbled_1: pin names not known; wires that end beside it: in1, in1

  assign U = in1;

  // Other names for the same wires on the sheet: zz[7:0] = in8

  // Notes on the sheet:
  //   All Components available in Digital
endmodule
